# Fritzing sketch test-gpio (saved by Fritzing 0.9.2b)

parts:
  Raspberry_Pi1 = Raspberry Pi B rev2

nets:
  N1: Raspberry_Pi1.GPIO_23, Raspberry_Pi1.GPIO_22
  N2: Raspberry_Pi1.GPIO_17, Raspberry_Pi1.GPIO_18
  N3: Raspberry_Pi1.GPIO_27, Raspberry_Pi1.GPIO_4
  N4: Raspberry_Pi1.GPIO_24, Raspberry_Pi1.GPIO_25
